# Fritzing sketch CANSAT MICRO SD (saved by Fritzing 0.9.3b)

parts:
  GY1 = MPU-6050 Board GY-521 [form="♀ (female)" package=THT]
  Componente1 = BMP180 Breakout (GY-68)
  Componente2 = Arduino Nano (Rev3.0)
  Componente3 = MicroSD Card Module

nets:
  N1: GY1.pin1, Componente2.5V
  N2: GY1.pin2, Componente2.GND
  N3: GY1.pin3, Componente2.A5
  N4: GY1.pin4, Componente2.A4
  VCC: Componente1.VCC, Componente2.3V3
  N5: Componente2.D6, Componente3.CS
  N6: Componente2.D11/MOSI, Componente3.MOSI
  N7: Componente2.D12/MISO, Componente3.MISO
  N8: Componente2.D13/SCK, Componente3.SCK

custom parts:
  MPU-6050 Board GY-521: Acelerometro y Giroscopio MPU-6050 Board GY-521
  BMP180 Breakout (GY-68): This is a simple breakout board for the BMP180, a high-precision, low-power barometric pressure sensor made by Bosch Sensortec. The range of measurement is from 300hPa to 1100hPa. The sensor can be supplied with voltage ranging from 1.8V to 3.6V. Operating temperature range is -40 to +85 °C. This particular breakout board (or perhaps the configuration) is produced by Shenzhen Keep Power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
