# Fritzing sketch CANSAT NRF24L01 (saved by Fritzing 0.9.3b)

parts:
  Componente1 = Arduino Uno (Rev3)
  Componente2 = NRF24L01+ Breakout Board
  C1 = Electrolytic Capacitor [capacitance=10μF package="0605 [SMD, electrolytic]"]
  Componente5 = NRF24L01+ Breakout Board
  C2 = Electrolytic Capacitor [capacitance=10μF package="0605 [SMD, electrolytic]"]
  VCC1 = Battery block 9V
  Componente7 = BMP180 Breakout (GY-68)
  Componente8 = Arduino Nano (Rev3.0)

nets:
  N1: Componente1.D9_PWM, Componente2.CE
  N2: Componente1.D10_PWM/SS, Componente2.CS
  N3: Componente1.D11_PWM/MOSI, Componente2.MOSI
  N4: Componente1.D12/MISO, Componente2.MISO
  N5: Componente1.D13/SCK, Componente2.SCK
  3V3: Componente1.3V3, Componente2.VCC, C1.+
  GND: Componente1.GND, Componente2.GND, C1.-
  GND_2: Componente5.GND, C2.-, Componente7.GND, Componente8.GND
  VCC: Componente5.VCC, C2.+, Componente8.3V3
  N6: Componente5.CE, Componente8.D9
  N7: Componente5.CS, Componente8.D10
  N8: Componente5.SCK, Componente8.D13/SCK
  N9: Componente5.MOSI, Componente8.D11/MOSI
  N10: Componente5.MISO, Componente8.D12/MISO
  N11: VCC1.+, Componente8.VIN
  N12: Componente7.SCL, Componente8.A5
  N13: Componente7.SDA, Componente8.A4

custom parts:
  BMP180 Breakout (GY-68): This is a simple breakout board for the BMP180, a high-precision, low-power barometric pressure sensor made by Bosch Sensortec. The range of measurement is from 300hPa to 1100hPa. The sensor can be supplied with voltage ranging from 1.8V to 3.6V. Operating temperature range is -40 to +85 °C. This particular breakout board (or perhaps the configuration) is produced by Shenzhen Keep Power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
